// Logisim project project.circ as structural Verilog: 7 circuits, main circuit main
module main (
  input  in_1,
  input  in_2,
  output [31:0] out_3,
  output [31:0] out_4,
  output [31:0] out_5,
  output [7:0] out_6,
  output [31:0] out_7,
  output [31:0] out_8,
  output [4:0] rs,
  output [4:0] rt,
  output [4:0] rd,
  output [3:0] opcode,
  output [31:0] out_13
);

  wire alusrc, and_1_out, and_2_out, clk, clock_1_out, d_ff_1_q, jmp, li, lw, memtoRegmux, Move, sw,
       writeNable, writeNablePipe, writeNablePipeResul;
  wire [3:0] multiplexer_9_out;
  wire [4:0] multiplexer_3_out;
  wire [7:0] bit_extender_1_out, bit_extender_3_out, multiplexer_2_out;
  wire [31:0] adder_1_out, bit_extender_2_out, multiplexer_6_out, multiplexer_7_out, ram_1_dout, regcpu_1_r1,
       regcpu_1_r2, register_1_q, v0;

  Register #(.width(32)) register_1 (
    .D(adder_1_out), .clk(clk), .Q({register_1_q[31:10], out_6, register_1_q[1:0]}), .clr(in_1));  // open: en
  Adder #(.width(32)) adder_1 (
    .a(32'h4), .b({register_1_q[31:10], out_6, register_1_q[1:0]}), .out(adder_1_out));  // open: cin, cout
  Multiplexer multiplexer_1 (.in0(clock_1_out), .in1(1'b1), .out(clk), .sel(in_2));
  Clock clock_1 (.out(clock_1_out));
  assign bit_extender_1_out = {{3{out_3[27]}}, out_3[27:23]};  // Bit_Extender bit_extender_1
  Multiplexer #(.width(8)) multiplexer_2 (.in0(out_6), .in1(bit_extender_1_out), .out(multiplexer_2_out), .sel(jmp));
  ROM #(.dataWidth(32)) rom_1 (.addr(multiplexer_2_out), .data(out_5));
  UC uc_1 (
    .op0(opcode[3]), .op1(opcode[2]), .op2(opcode[1]), .op3(opcode[0]), .ALUsrc(alusrc), .lw(lw), .li(li),
    .sw(sw), .Jump(jmp), .Move(Move), .RegWrite(writeNable), .MemRead(memtoRegmux), .MemWrite(sw));
  MulDecode muldecode_1 (.ifenter(out_5[31:28]), .ifout(writeNablePipe));
  Multiplexer #(.width(5)) multiplexer_3 (.in0(out_3[17:13]), .in1({5{1'b0}}), .out(multiplexer_3_out), .sel(li));
  Multiplexer multiplexer_4 (.in0(writeNable), .in1(writeNablePipe), .out(writeNablePipeResul), .sel(writeNablePipe));
  Multiplexer #(.width(32)) multiplexer_5 (.in0(v0), .in1(out_5), .out(v0), .sel(writeNablePipe));
  Multiplexer #(.width(32)) multiplexer_6 (.in0(out_4), .in1(bit_extender_2_out), .out(multiplexer_6_out), .sel(li));
  assign bit_extender_2_out = {{27{out_3[27]}}, out_3[27:23]};  // Bit_Extender bit_extender_2
  and and_1 (and_1_out, opcode[3], opcode[2], ~opcode[1], ~opcode[0]);  // AND_Gate
  Multiplexer #(.width(32)) multiplexer_7 (
    .in0(out_5), .in1({32{1'b0}}), .out(multiplexer_7_out), .sel(writeNablePipe));
  Multiplexer #(.width(32)) multiplexer_8 (
    .in0(multiplexer_7_out), .in1({32{1'b0}}), .out({opcode, out_3[27:0]}), .sel(d_ff_1_q));
  assign bit_extender_3_out = {{3{1'b0}}, out_3[27:23]};  // Bit_Extender bit_extender_3
  D_Flip_Flop d_ff_1 (.D(writeNablePipe), .clk(clk), .Q(d_ff_1_q));  // open: Qn, preset, reset
  regCPU regcpu_1 (
    .Move(Move), .WriteEnable(writeNablePipeResul), .Clock(clk), .DataIncome(multiplexer_6_out),
    .Entry1(multiplexer_3_out), .Entry2(out_3[22:18]), .RegEntry(out_3[27:23]), .a0(v0), .v0(v0),
    .R1(regcpu_1_r1), .R2(regcpu_1_r2));
  Multiplexer #(.width(4)) multiplexer_9 (.in0(4'b1111), .in1(opcode), .out(multiplexer_9_out), .sel(alusrc));
  ULA ula_1 (.aluOP(multiplexer_9_out), .entry1(regcpu_1_r1), .entry2(regcpu_1_r2), .result1(out_13), .result2(out_8));
  Multiplexer #(.width(32)) multiplexer_10 (.in0(out_13), .in1(regcpu_1_r1), .out(out_7), .sel(and_2_out));
  and and_2 (and_2_out, sw, ~and_1_out);  // AND_Gate
  RAM #(.dataWidth(32)) ram_1 (.addr(bit_extender_3_out), .we(sw), .oe(lw), .clk(clk), .din(out_7), .dout(ram_1_dout));
  Multiplexer #(.width(32)) multiplexer_11 (.in0(out_7), .in1(ram_1_dout), .out(out_4), .sel(memtoRegmux));

  assign out_3[31:28] = opcode;
  assign rd = out_3[27:23];
  assign rs = out_3[17:13];
  assign rt = out_3[22:18];

  // Other names for the same wires on the sheet: datain[31:0] = out_4; adr[4:0] = out_3[27:23]; stop = in_2

  // Notes on the sheet:
  //   contents of rom_1 (hex, n*v repeats v):
  //   9fffffff 12342233 bf0fa111 9fffffff 12342233 bff1a111 c0fdf1aa 9fffffff 32145211 bf0fa111 9fffffff
  //   12342233 bff1a111 c1fdf1aa
endmodule

module ULA (
  input  [3:0] aluOP,
  input  [31:0] entry1,
  input  [31:0] entry2,
  output [31:0] result1,
  output [31:0] result2
);

  wire comparator_1_gt, equal;
  wire [31:0] adder_1_out, and_1_out, bit_extender_1_out, multiplier_1_out, or_1_out, shifter_1_out,
       shifter_2_out, subtractor_1_out, xor_1_out;

  Shifter #(.width(32)) shifter_1 (.in(entry1), .\dist (entry2[4:0]), .out(shifter_1_out));
  Shifter #(.shift("ar"), .width(32)) shifter_2 (.in(entry1), .\dist (entry2[4:0]), .out(shifter_2_out));
  Multiplier #(.width(32)) multiplier_1 (.a(entry1), .b(entry2), .out(multiplier_1_out));  // open: cin, cout
  Adder #(.width(32)) adder_1 (.a(entry1), .b(entry2), .out(adder_1_out));  // open: cin, cout
  Subtractor #(.width(32)) subtractor_1 (.a(entry1), .b(entry2), .out(subtractor_1_out));  // open: bin, bout
  assign and_1_out = entry1 & entry2;  // AND_Gate and_1, 32 bits wide
  assign or_1_out = entry1 | entry2;  // OR_Gate or_1, 32 bits wide
  assign xor_1_out = entry1 ^ entry2;  // XOR_Gate xor_1, 32 bits wide
  Comparator #(.width(32)) comparator_1 (.a(entry1), .b(entry2), .gt(comparator_1_gt), .eq(equal));  // open: lt
  Multiplier #(.width(4)) multiplier_2 (.a(entry1[3:0]), .b(entry2[3:0]), .out(result2[3:0]));  // open: cin, cout
  Multiplier #(.width(4)) multiplier_3 (.a(entry1[7:4]), .b(entry2[7:4]), .out(result2[7:4]));  // open: cin, cout
  Multiplier #(.width(4)) multiplier_4 (.a(entry1[11:8]), .b(entry2[11:8]), .out(result2[11:8]));  // open: cin, cout
  Multiplier #(.width(4)) multiplier_5 (.a(entry1[15:12]), .b(entry2[15:12]), .out(result2[15:12]));  // open: cin, cout
  Multiplier #(.width(4)) multiplier_6 (.a(entry1[19:16]), .b(entry2[19:16]), .out(result2[19:16]));  // open: cin, cout
  Multiplier #(.width(4)) multiplier_7 (.a(entry1[23:20]), .b(entry2[23:20]), .out(result2[23:20]));  // open: cin, cout
  Multiplier #(.width(4)) multiplier_8 (.a(entry1[27:24]), .b(entry2[27:24]), .out(result2[27:24]));  // open: cin, cout
  Multiplier #(.width(4)) multiplier_9 (.a(entry1[31:28]), .b(entry2[31:28]), .out(result2[31:28]));  // open: cin, cout
  assign bit_extender_1_out = {{31{comparator_1_gt}}, comparator_1_gt};  // Bit_Extender bit_extender_1
  Multiplexer #(.select(4), .width(32)) multiplexer_1 (
    .in0(shifter_1_out), .in1(shifter_2_out), .in2(multiplier_1_out), .in3(adder_1_out),
    .in4(subtractor_1_out), .in5(and_1_out), .in6(or_1_out), .in7(xor_1_out), .in8(bit_extender_1_out),
    .in9(result2), .in10({32{1'b0}}), .in11(result2), .in12(result2), .in13({32{1'b0}}), .in14({32{1'b0}}),
    .in15({32{1'b0}}), .out(result1), .sel(aluOP));

  // Other names for the same wires on the sheet: entryX[31:0] = entry1; entryY[31:0] = entry2; y5[4:0] = entry2[4:0];
  //   Resul1[31:0] = result1; Resul2[31:0] = result2

  // Notes on the sheet:
  //   OUTPUT
endmodule

module PC (
  input  clk,
  input  reset,
  output [7:0] out_3
);

  wire [31:0] adder_1_out, register_1_q;

  Adder #(.width(32)) adder_1 (
    .a(32'h4), .b({register_1_q[31:10], out_3, register_1_q[1:0]}), .out(adder_1_out));  // open: cin, cout
  Register #(.width(32)) register_1 (
    .D(adder_1_out), .clk(clk), .Q({register_1_q[31:10], out_3, register_1_q[1:0]}), .clr(reset));  // open: en
endmodule

// MUXREG1
module BancoDeRegistradores (
  input  [2:0] READ1,
  input  [2:0] READ2,
  input  clear,
  input  clk,
  input  [31:0] Data,
  input  [2:0] REGEnable,
  input  WriteEnable,
  output [31:0] RD1,
  output [31:0] RD2
);

  wire enaREG0, enaREG1, enaREG2, enaREG3, enaREG4, enaREG5, enaREG6, enaREG7;
  wire [31:0] demultiplexer_1_out0, demultiplexer_1_out1, demultiplexer_1_out2, demultiplexer_1_out3,
       demultiplexer_1_out4, demultiplexer_1_out5, demultiplexer_1_out6, demultiplexer_1_out7, MUXREG0,
       MUXREG1, MUXREG2, MUXREG3, MUXREG4, MUXREG5, MUXREG6, MUXREG7;

  Multiplexer #(.select(3), .width(32)) multiplexer_1 (
    .in0(MUXREG0), .in1(MUXREG1), .in2(MUXREG2), .in3(MUXREG3), .in4(MUXREG4), .in5(MUXREG5), .in6(MUXREG6),
    .in7(MUXREG7), .out(RD1), .sel(READ1));
  Multiplexer #(.select(3), .width(32)) multiplexer_2 (
    .in0(MUXREG0), .in1(MUXREG1), .in2(MUXREG2), .in3(MUXREG3), .in4(MUXREG4), .in5(MUXREG5), .in6(MUXREG6),
    .in7(MUXREG7), .out(RD2), .sel(READ2));
  Demultiplexer #(.select(3), .width(32)) demultiplexer_1 (
    .out0(demultiplexer_1_out0), .out1(demultiplexer_1_out1), .out2(demultiplexer_1_out2),
    .out3(demultiplexer_1_out3), .out4(demultiplexer_1_out4), .out5(demultiplexer_1_out5),
    .out6(demultiplexer_1_out6), .out7(demultiplexer_1_out7), .in(Data), .sel(REGEnable));
  Demultiplexer #(.select(3)) demultiplexer_2 (
    .out0(enaREG0), .out1(enaREG1), .out2(enaREG2), .out3(enaREG3), .out4(enaREG4), .out5(enaREG5),
    .out6(enaREG6), .out7(enaREG7), .in(WriteEnable), .sel(REGEnable));
  Register #(.width(32)) REG0 (.D(demultiplexer_1_out0), .en(enaREG0), .clk(clk), .Q(MUXREG0), .clr(clear));
  Register #(.width(32)) REG1 (.D(demultiplexer_1_out1), .en(enaREG1), .clk(clk), .Q(MUXREG1), .clr(clear));
  Register #(.width(32)) REG2 (.D(demultiplexer_1_out2), .en(enaREG2), .clk(clk), .Q(MUXREG2), .clr(clear));
  Register #(.width(32)) REG3 (.D(demultiplexer_1_out3), .en(enaREG3), .clk(clk), .Q(MUXREG3), .clr(clear));
  Register #(.width(32)) REG4 (.D(demultiplexer_1_out4), .en(enaREG4), .clk(clk), .Q(MUXREG4), .clr(clear));
  Register #(.width(32)) REG5 (.D(demultiplexer_1_out5), .en(enaREG5), .clk(clk), .Q(MUXREG5), .clr(clear));
  Register #(.width(32)) REG6 (.D(demultiplexer_1_out6), .en(enaREG6), .clk(clk), .Q(MUXREG6), .clr(clear));
  Register #(.width(32)) REG7 (.D(demultiplexer_1_out7), .en(enaREG7), .clk(clk), .Q(MUXREG7));  // open: clr
endmodule

module UC (
  input  op0,
  input  op1,
  input  op2,
  input  op3,
  output ALUsrc,
  output lw,
  output li,
  output sw,
  output Jump,
  output Move,
  output RegWrite,
  output MemRead,
  output MemWrite
);

  wire and_1_out, and_2_out, and_3_out, and_4_out, and_6_out, and_7_out, and_10_out, and_11_out, not_1_out,
       not_2_out, not_3_out, not_4_out;

  not not_1 (not_1_out, op0);
  not not_2 (not_2_out, op1);
  not not_3 (not_3_out, op2);
  not not_4 (not_4_out, op3);
  and and_1 (and_1_out, not_2_out, not_3_out);
  and and_2 (and_2_out, not_3_out, not_4_out);
  and and_3 (and_3_out, op0, not_2_out, not_3_out, op3);
  and and_4 (and_4_out, op0, op1, op2, op3);
  and and_5 (li, op0, op1, not_3_out, op3);
  and and_6 (and_6_out, op0, not_2_out, op3);
  and and_7 (and_7_out, op0, op1, not_4_out);
  and and_8 (Move, op0, not_2_out, op2, op3);
  or or_1 (RegWrite, not_1_out, not_2_out, op3);
  and and_9 (MemRead, op0, op1, op2, op3);
  and and_10 (and_10_out, op0, not_2_out, op2, op3);
  and and_11 (and_11_out, op0, op1, not_4_out);
  or or_2 (ALUsrc, not_1_out, and_1_out, and_2_out);
  or or_3 (lw, and_3_out, and_4_out);
  or or_4 (sw, and_6_out, and_7_out);
  or or_5 (MemWrite, and_10_out, and_11_out);

  assign Jump = 1'b0;
endmodule

module regCPU (
  input  Move,
  input  WriteEnable,
  input  Clock,
  input  [31:0] DataIncome,
  input  [4:0] Entry1,
  input  [4:0] Entry2,
  input  [4:0] RegEntry,
  input  [31:0] a0,
  input  [31:0] v0,
  output [31:0] R1,
  output [31:0] R2
);

  wire demultiplexer_1_out0, demultiplexer_1_out1, demultiplexer_1_out2, demultiplexer_1_out3,
       demultiplexer_1_out4, demultiplexer_1_out5, demultiplexer_1_out6, demultiplexer_1_out7,
       demultiplexer_1_out8, demultiplexer_1_out9, demultiplexer_1_out10, demultiplexer_1_out11,
       demultiplexer_1_out12, demultiplexer_1_out13, demultiplexer_1_out14, demultiplexer_1_out15,
       demultiplexer_1_out16, demultiplexer_1_out17, demultiplexer_1_out18, demultiplexer_1_out19,
       demultiplexer_1_out20, demultiplexer_1_out21, demultiplexer_1_out22, demultiplexer_1_out23,
       demultiplexer_1_out24, demultiplexer_1_out25, demultiplexer_1_out26, demultiplexer_1_out27,
       demultiplexer_1_out28, demultiplexer_1_out29, demultiplexer_1_out30, demultiplexer_1_out31, undriven;
  wire [31:0] a1_q, a2_q, a3_q, at_q, b, multiplexer_2_out, reg1, register_22_q, register_23_q,
       register_24_q, register_25_q, register_26_q, register_27_q, register_28_q, register_29_q,
       register_30_q, register_31_q, register_32_q, register_33_q, register_34_q, register_35_q,
       register_36_q, register_37_q, register_38_q, register_39_q, register_40_q, register_41_q,
       register_43_q, register_44_q, v1_q, zero_q;

  Multiplexer #(.width(32)) multiplexer_1 (.in0(reg1), .in1(v0), .out(R1), .sel(Move));
  Register #(.width(32)) Zerado ();  // open: D, en, Q, clk, clr
  Register #(.width(32)) register_1 ();  // open: D, en, Q, clk, clr
  Register #(.width(32)) t0 ();  // open: D, en, Q, clk, clr
  Register #(.width(32)) t1 ();  // open: D, en, Q, clk, clr
  Register #(.width(32)) register_2 ();  // open: D, en, Q, clk, clr
  Register #(.width(32)) register_3 ();  // open: D, en, Q, clk, clr
  Register #(.width(32)) t8 ();  // open: D, en, Q, clk, clr
  Register #(.width(32)) t9 ();  // open: D, en, Q, clk, clr
  Register #(.width(32)) register_4 ();  // open: D, en, Q, clk, clr
  Register #(.width(32)) t2 ();  // open: D, en, Q, clk, clr
  Register #(.width(32)) register_5 ();  // open: D, en, Q, clk, clr
  Register #(.width(32)) register_6 ();  // open: D, en, Q, clk, clr
  Register #(.width(32)) azero ();  // open: D, en, Q, clk, clr
  Register #(.width(32)) vzero ();  // open: D, en, Q, clk, clr
  Register #(.width(32)) register_7 ();  // open: D, en, Q, clk, clr
  Register #(.width(32)) register_8 ();  // open: D, en, Q, clk, clr
  Register #(.width(32)) t3 ();  // open: D, en, Q, clk, clr
  Register #(.width(32)) t4 ();  // open: D, en, Q, clk, clr
  Register #(.width(32)) register_9 ();  // open: D, en, Q, clk, clr
  Register #(.width(32)) register_10 (.clr(undriven));  // open: D, en, Q, clk
  Register #(.width(32)) register_11 ();  // open: D, en, Q, clk, clr
  Register #(.width(32)) register_12 ();  // open: D, en, Q, clk, clr
  Register #(.width(32)) register_13 ();  // open: D, en, Q, clk, clr
  Register #(.width(32)) t5 ();  // open: D, en, Q, clk, clr
  Register #(.width(32)) register_14 ();  // open: D, en, Q, clk, clr
  Register #(.width(32)) register_15 ();  // open: D, en, Q, clk, clr
  Multiplexer #(.width(32)) multiplexer_2 (.in0(v0), .in1(DataIncome), .out(multiplexer_2_out), .sel(Move));
  Register #(.width(32)) register_16 ();  // open: D, en, Q, clk, clr
  Register #(.width(32)) register_17 ();  // open: D, en, Q, clk, clr
  Register #(.width(32)) t6 ();  // open: D, en, Q, clk, clr
  Register #(.width(32)) t7 ();  // open: D, en, Q, clk, clr
  Register #(.width(32)) register_18 ();  // open: D, en, Q, clk, clr
  Register #(.width(32)) register_19 ();  // open: D, en, Q, clk, clr
  Register #(.width(32)) register_20 ();  // open: D, en, Q, clk, clr
  Register #(.width(32)) register_21 ();  // open: D, en, Q, clk, clr
  Demultiplexer #(.enable("true"), .select(5)) demultiplexer_1 (
    .out0(demultiplexer_1_out0), .out1(demultiplexer_1_out1), .out2(demultiplexer_1_out2),
    .out3(demultiplexer_1_out3), .out4(demultiplexer_1_out4), .out5(demultiplexer_1_out5),
    .out6(demultiplexer_1_out6), .out7(demultiplexer_1_out7), .out8(demultiplexer_1_out8),
    .out9(demultiplexer_1_out9), .out10(demultiplexer_1_out10), .out11(demultiplexer_1_out11),
    .out12(demultiplexer_1_out12), .out13(demultiplexer_1_out13), .out14(demultiplexer_1_out14),
    .out15(demultiplexer_1_out15), .out16(demultiplexer_1_out16), .out17(demultiplexer_1_out17),
    .out18(demultiplexer_1_out18), .out19(demultiplexer_1_out19), .out20(demultiplexer_1_out20),
    .out21(demultiplexer_1_out21), .out22(demultiplexer_1_out22), .out23(demultiplexer_1_out23),
    .out24(demultiplexer_1_out24), .out25(demultiplexer_1_out25), .out26(demultiplexer_1_out26),
    .out27(demultiplexer_1_out27), .out28(demultiplexer_1_out28), .out29(demultiplexer_1_out29),
    .out30(demultiplexer_1_out30), .out31(demultiplexer_1_out31), .in(1'b1), .sel(RegEntry), .en(WriteEnable));
  Register #(.width(32)) zero (.D(DataIncome), .en(demultiplexer_1_out0), .Q(zero_q));  // open: clk, clr
  Register #(.width(32)) register_22 (
    .D(DataIncome), .en(demultiplexer_1_out8), .Q(register_22_q), .clk(Clock));  // open: clr
  Register #(.width(32)) register_23 (
    .D(DataIncome), .en(demultiplexer_1_out16), .Q(register_23_q), .clk(Clock));  // open: clr
  Register #(.width(32)) register_24 (
    .D(DataIncome), .en(demultiplexer_1_out24), .Q(register_24_q), .clk(Clock));  // open: clr
  Register #(.width(32)) at (.D(DataIncome), .en(demultiplexer_1_out1), .Q(at_q), .clk(Clock));  // open: clr
  Register #(.width(32)) register_25 (
    .D(DataIncome), .en(demultiplexer_1_out9), .Q(register_25_q), .clk(Clock));  // open: clr
  Register #(.width(32)) register_26 (
    .D(DataIncome), .en(demultiplexer_1_out17), .Q(register_26_q), .clk(Clock));  // open: clr
  Register #(.width(32)) register_27 (
    .D(DataIncome), .en(demultiplexer_1_out25), .Q(register_27_q), .clk(Clock));  // open: clr
  Register #(.width(32)) register_28 (
    .D(DataIncome), .en(demultiplexer_1_out10), .Q(register_28_q), .clk(Clock));  // open: clr
  Register #(.width(32)) register_29 (
    .D(DataIncome), .en(demultiplexer_1_out18), .Q(register_29_q), .clk(Clock));  // open: clr
  Register #(.width(32)) register_30 (
    .D(DataIncome), .en(demultiplexer_1_out26), .Q(register_30_q), .clk(Clock));  // open: clr
  Register #(.width(32)) v1 (.D(DataIncome), .en(demultiplexer_1_out3), .Q(v1_q), .clk(Clock));  // open: clr
  Register #(.width(32)) register_31 (
    .D(DataIncome), .en(demultiplexer_1_out11), .Q(register_31_q), .clk(Clock));  // open: clr
  Register #(.width(32)) register_32 (
    .D(DataIncome), .en(demultiplexer_1_out19), .Q(register_32_q), .clk(Clock));  // open: clr
  Register #(.width(32)) register_33 (
    .D(DataIncome), .en(demultiplexer_1_out27), .Q(register_33_q), .clk(Clock));  // open: clr
  Register #(.width(32)) register_34 (
    .D(DataIncome), .en(demultiplexer_1_out12), .Q(register_34_q), .clk(Clock));  // open: clr
  Register #(.width(32)) register_35 (
    .D(DataIncome), .en(demultiplexer_1_out20), .Q(register_35_q), .clk(Clock));  // open: clr
  Register #(.width(32)) register_36 (
    .D(DataIncome), .en(demultiplexer_1_out28), .Q(register_36_q), .clk(Clock));  // open: clr
  Register #(.width(32)) a1 (.D(DataIncome), .en(demultiplexer_1_out5), .Q(a1_q), .clk(Clock));  // open: clr
  Register #(.width(32)) register_37 (
    .D(DataIncome), .en(demultiplexer_1_out13), .Q(register_37_q), .clk(Clock));  // open: clr
  Register #(.width(32)) register_38 (
    .D(DataIncome), .en(demultiplexer_1_out21), .Q(register_38_q), .clk(Clock));  // open: clr
  Register #(.width(32)) register_39 (
    .D(DataIncome), .en(demultiplexer_1_out29), .Q(register_39_q), .clk(Clock));  // open: clr
  Register #(.width(32)) a2 (.D(DataIncome), .en(demultiplexer_1_out6), .Q(a2_q), .clk(Clock));  // open: clr
  Register #(.width(32)) register_40 (
    .D(DataIncome), .en(demultiplexer_1_out14), .Q(register_40_q), .clk(Clock));  // open: clr
  Register #(.width(32)) register_41 (
    .D(DataIncome), .en(demultiplexer_1_out22), .Q(register_41_q), .clk(Clock));  // open: clr
  Register #(.width(32)) register_42 (.D(DataIncome), .en(demultiplexer_1_out30), .Q(b), .clk(Clock));  // open: clr
  Register #(.width(32)) a3 (.D(DataIncome), .en(demultiplexer_1_out7), .Q(a3_q), .clk(Clock));  // open: clr
  Register #(.width(32)) register_43 (
    .D(DataIncome), .en(demultiplexer_1_out23), .Q(register_43_q), .clk(Clock));  // open: clr
  Register #(.width(32)) register_44 (
    .D(DataIncome), .en(demultiplexer_1_out31), .Q(register_44_q), .clk(Clock));  // open: clr
  Multiplexer #(.select(5), .width(32)) multiplexer_3 (
    .in0(zero_q), .in1(at_q), .in2(v0), .in3(v1_q), .in4(a0), .in5(a1_q), .in6(a2_q), .in7(a3_q),
    .in8(register_22_q), .in9(register_25_q), .in10(register_28_q), .in11(register_31_q),
    .in12(register_34_q), .in13(register_37_q), .in14(register_40_q), .in15(b), .in16(register_23_q),
    .in17(register_26_q), .in18(register_29_q), .in19(register_32_q), .in20(register_35_q),
    .in21(register_38_q), .in22(register_41_q), .in23(register_43_q), .in24(register_24_q),
    .in25(register_27_q), .in26(register_30_q), .in27(register_33_q), .in28(register_36_q),
    .in29(register_39_q), .in30(b), .in31(register_44_q), .out(reg1), .sel(Entry1));
  Multiplexer #(.select(5), .width(32)) multiplexer_4 (
    .in0(zero_q), .in1(at_q), .in2(v0), .in3(v1_q), .in4(a0), .in5(a1_q), .in6(a2_q), .in7(a3_q),
    .in8(register_22_q), .in9(register_25_q), .in10(register_28_q), .in11(register_31_q),
    .in12(register_34_q), .in13(register_37_q), .in14(register_40_q), .in15(b), .in16(register_23_q),
    .in17(register_26_q), .in18(register_29_q), .in19(register_32_q), .in20(register_35_q),
    .in21(register_38_q), .in22(register_41_q), .in23(register_43_q), .in24(register_24_q),
    .in25(register_27_q), .in26(register_30_q), .in27(register_33_q), .in28(register_36_q),
    .in29(register_39_q), .in30(b), .in31(register_44_q), .out(R2), .sel(Entry2));

  // Other names for the same wires on the sheet: clk = Clock; iReg1[4:0] = Entry1; iReg2[4:0] = Entry2;
  //   reg2[31:0] = R2; we = WriteEnable; a[31:0] = DataIncome; write_data[31:0] = DataIncome;
  //   write_reg[4:0] = RegEntry

  // Notes on the sheet:
  //   OUTPUT
endmodule

module MulDecode (
  input  [3:0] ifenter,
  output ifout
);

  wire [6:0] multiplier_9_out, multiplier_10_out, multiplier_11_out, multiplier_12_out, undriven_2,
       undriven_3, undriven_4;
  wire [27:0] undriven;
  wire [27:21] undriven_5;
  wire [31:0] entryX, entryY, Resul2;

  Multiplexer #(.select(4)) multiplexer_1 (
    .in0(1'b0), .in1(1'b0), .in2(1'b0), .in3(1'b0), .in4(1'b0), .in5(1'b0), .in6(1'b0), .in7(1'b0),
    .in8(1'b0), .in9(1'b1), .in10(1'b0), .in11(1'b0), .in12(1'b0), .in13(1'b0), .in14(1'b0), .in15(1'b0),
    .out(ifout), .sel(ifenter));
  Multiplier #(.width(4)) multiplier_1 (.a(entryY[31:28]), .b(entryX[31:28]), .out(Resul2[3:0]));  // open: cin, cout
  Multiplier #(.width(4)) multiplier_2 (.a(entryY[27:24]), .b(entryX[27:24]), .out(Resul2[7:4]));  // open: cin, cout
  Multiplier #(.width(4)) multiplier_3 (.a(entryY[23:20]), .b(entryX[23:20]), .out(Resul2[11:8]));  // open: cin, cout
  Multiplier #(.width(4)) multiplier_4 (.a(entryY[19:16]), .b(entryX[19:16]), .out(Resul2[15:12]));  // open: cin, cout
  Multiplier #(.width(4)) multiplier_5 (.a(entryY[15:12]), .b(entryX[15:12]), .out(Resul2[19:16]));  // open: cin, cout
  Multiplier #(.width(4)) multiplier_6 (.a(entryY[11:8]), .b(entryX[11:8]), .out(Resul2[23:20]));  // open: cin, cout
  Multiplier #(.width(4)) multiplier_7 (.a(entryY[7:4]), .b(entryX[7:4]), .out(Resul2[27:24]));  // open: cin, cout
  Multiplier #(.width(4)) multiplier_8 (.a(entryY[3:0]), .b(entryX[3:0]), .out(Resul2[31:28]));  // open: cin, cout
  Multiplier #(.width(7)) multiplier_9 (
    .a(undriven_5), .b(undriven[27:21]), .out(multiplier_9_out));  // open: cin, cout
  Multiplier #(.width(7)) multiplier_10 (
    .a(undriven_4), .b(undriven[20:14]), .out(multiplier_10_out));  // open: cin, cout
  Multiplier #(.width(7)) multiplier_11 (
    .a(undriven_3), .b(undriven[13:7]), .out(multiplier_11_out));  // open: cin, cout
  Multiplier #(.width(7)) multiplier_12 (
    .a(undriven_2), .b(undriven[6:0]), .out(multiplier_12_out));  // open: cin, cout
endmodule
